# Fritzing sketch frtizing_diagram (saved by Fritzing 0.9.4)
breadboards: 2

parts:
  U1 = WS2812 RGB LED strip
  U2 = WS2812 RGB LED strip
  U3 = WS2812 RGB LED strip
  C7 = Electrolytic Capacitor [capacitance=1000µF package="300 mil [THT, electrolytic]"]
  JACK1 = 2.1mm Barrel Jack with Terminal Block
  Keypad4x1 = Membrane Keypad 4x4  # not connected
  Part2 = Arduino Micro (Rev3)  # not connected
  R1 = Resistor [tolerance=±5% resistance=330 package="2010 [SMD]"]

nets:
  N1: U1.GND#0, U2.GND#4
  N2: U1.VCC#1, U2.VCC#5
  N3: U1.DIN, U2.DOUT
  N4: U1.GND#4, U3.GND, C7.-, JACK1.NEG
  N5: U1.VCC#5, U3.VCC, C7.+, JACK1.POS
  N6: U1.DOUT, U3.DIN
  N7: U2.DIN, R1.Pin_1

notes:
  Disconnect the 5V from the Arduino prior to plugging in the USB to your PC
  When both power sources are connected the Arduino should be the last unplugged and the first unplugged

custom parts:
  WS2812 RGB LED strip: WS2812 strip
  Membrane Keypad 4x4: 4x4 Matrix Membrane Keypad
